// Logisim project Ctl_Load_Store.circ as structural Verilog: 1 circuit, main circuit Load_Store
module Load_Store (
  input  Enable,
  input  [15:0] Instruction,
  input  Clk,
  input  Reset,
  input  [31:0] Stack_Pointer,
  output Store,
  output Load,
  output PC_Hold,
  output [2:0] Rmd,
  output [31:0] RAM_Addr
);

  wire and_1_out, and_2_out, d_ff_1_q, d_ff_1_qn, load_inter, load_t, not_1_out, not_2_out, pc_hold_inter,
       store_t;
  wire [31:0] bit_extender_1_out, multiplier_1_out, ram_addr_t;

  Demultiplexer demultiplexer_1 (.out0(store_t), .out1(load_t), .in(1'b1), .sel(and_1_out));
  and and_1 (and_1_out, Instruction[11], 1'b1);
  assign bit_extender_1_out = {{24{1'b0}}, Instruction[7:0]};  // Bit_Extender bit_extender_1
  Multiplier #(.mode("twosComplement"), .width(32)) multiplier_1 (
    .a(bit_extender_1_out), .b(32'h4), .out(multiplier_1_out));  // open: cin, cout
  Adder #(.width(32)) adder_1 (.a(Stack_Pointer), .b(multiplier_1_out), .out(ram_addr_t));  // open: cin, cout
  and and_2 (and_2_out, d_ff_1_q, load_t);
  D_Flip_Flop #(.trigger("falling")) d_ff_1 (
    .D(not_1_out), .clk(Clk), .Q(d_ff_1_q), .Qn(d_ff_1_qn), .reset(Reset));  // open: preset
  not not_1 (not_1_out, and_2_out);
  and and_3 (Store, Enable, store_t);
  and and_4 (Load, Enable, load_inter);
  and and_5 (PC_Hold, Enable, pc_hold_inter);
  Multiplexer #(.width(3)) multiplexer_1 (.in0(3'b000), .in1(Instruction[10:8]), .out(Rmd), .sel(Enable));
  Multiplexer #(.width(32)) multiplexer_2 (.in0({32{1'b0}}), .in1(ram_addr_t), .out(RAM_Addr), .sel(Enable));
  not not_2 (not_2_out, store_t);
  and and_6 (pc_hold_inter, not_2_out, d_ff_1_q);
  and and_7 (load_inter, not_2_out, d_ff_1_qn);

  // Other names for the same wires on the sheet: clock = Clk; imm8[7:0] = Instruction[7:0];
  //   rmd_t[2:0] = Instruction[10:8]; StoreOrLoadBit = Instruction[11]; load_out = Load; pc_hold_out = PC_Hold;
  //   ram_addr_out[31:0] = RAM_Addr; rmd_out[2:0] = Rmd; store_out = Store

  // Notes on the sheet:
  //   Instruction: pull=down
  //   Instruction decoder
  //   INPUT
  //   Ram_addr calculator
  //   OUTPUT
  //   Delay load and hold PC for 1 cycle for the RAM to send out requested data 
  //   THIS IS SIGNED MIGHT NEED TO BE CHANGED
endmodule
